# Fritzing sketch 11 (saved by Fritzing 0.9.1b)
breadboards: 1

parts:
  元件1 = Arduino Mega ADK (Rev3)
  U1 = LCD-16X2 [package=lcd-16x2]
  LCM1602_IIC1 = LCM1602 IIC [part_number="LCM1602 IIC" chip_label="LCM1602 IIC" package="DIP (Dual Inline) [THT]"]
  元件2 = Thumb Joystick
  元件3 = Thumb Joystick
  元件4 = Thumb Joystick
  Matrix_keypad1 = KEYPAD 4x4
  J1 = Basic Servo
  J2 = Basic Servo
  J3 = Basic Servo
  J4 = Basic Servo
  J5 = Basic Servo
  J6 = Basic Servo
  S1 = Pushbutton [package="[SMD]"]
  LED1 = smd LED [color="Red (633nm)" package="0805 [SMD]"]

nets:
  N1: 元件1.A0, 元件2.HORZ
  N2: 元件1.A1, 元件2.VERT
  N3: 元件1.A2, 元件3.HORZ
  N4: 元件1.A3, 元件3.VERT
  N5: 元件1.A4, 元件4.HORZ
  N6: 元件1.A5, 元件4.VERT
  N7: 元件1.D21/SCL, LCM1602_IIC1.SCL
  N8: 元件1.D20/SDA, LCM1602_IIC1.SDA
  N9: 元件1.D12_PWM, 元件2.SEL
  N10: 元件1.D11_PWM, 元件3.SEL
  N11: 元件1.D10_PWM, 元件4.SEL
  N12: 元件1.D9_PWM, Matrix_keypad1.col1
  N13: 元件1.D8_PWM, Matrix_keypad1.col2
  VCC: 元件1.5V, LCM1602_IIC1.VCC, 元件2.VCC, 元件3.VCC, 元件4.VCC, J5.vcc
  GND: 元件1.GND, LCM1602_IIC1.GND, 元件2.GND, 元件3.GND, 元件4.GND, J5.gnd, S1.Pin_1, S1.Pin_2, LED1.cathode
  N14: 元件1.D2_PWM, Matrix_keypad1.row4
  N15: 元件1.D3_PWM, Matrix_keypad1.row3
  N16: 元件1.D4_PWM, Matrix_keypad1.row2
  N17: 元件1.D5_PWM, Matrix_keypad1.row1
  N18: 元件1.D6_PWM, Matrix_keypad1.col4
  N19: 元件1.D7_PWM, Matrix_keypad1.col3
  N20: 元件1.D22, J6.pulse
  N21: 元件1.D23, J1.pulse
  N22: 元件1.D24, J2.pulse
  N23: 元件1.D25, J3.pulse
  N24: 元件1.D26, J4.pulse
  N25: 元件1.D27, J5.pulse
  N26: 元件1.D36, S1.Pin_3, S1.Pin_4
  N27: 元件1.D37, LED1.anode
  VSS: U1.VSS, LCM1602_IIC1.VSS
  VDD: U1.VDD, LCM1602_IIC1.VDD
  N28: U1.VO, LCM1602_IIC1.V0
  N29: U1.RS, LCM1602_IIC1.RS
  N30: U1.R_W, LCM1602_IIC1.RW
  N31: U1.E, LCM1602_IIC1.E
  N32: U1.DB0, LCM1602_IIC1.D0
  N33: U1.DB1, LCM1602_IIC1.D1
  N34: U1.DB2, LCM1602_IIC1.D2
  N35: U1.DB3, LCM1602_IIC1.D3
  N36: U1.DB4, LCM1602_IIC1.D4
  N37: U1.DB5, LCM1602_IIC1.D5
  N38: U1.DB6, LCM1602_IIC1.D6
  N39: U1.DB7, LCM1602_IIC1.D7
  N40: U1.A, LCM1602_IIC1.A
  N41: U1.K, LCM1602_IIC1.K

custom parts:
  LCM1602 IIC: I2C-Module to use a 1602 or 2004 LCD on with the wire.h libory Serial LCD Modul
  KEYPAD 4x4: Matrix keypad 16 buttons, 4 rows x 4 columns
